# Fritzing sketch Sketch (saved by Fritzing 0.9.2b)
breadboards: 1

parts:
  Part1 = Arduino Uno (Rev3)
  RHT1 = Humidity and Temperature Sensor RHT03
  NRF24L1 = NRF24L01

nets:
  N1: Part1.A4/SDA, RHT1.GND_2
  N2: Part1.D8, NRF24L1.CSN
  N3: Part1.D2, RHT1.GND_1
  N4: Part1.D7, NRF24L1.CE
  3V3: Part1.3V3, NRF24L1.VCC
  GND: Part1.GND, NRF24L1.GND

notes:
  nRF24L01 Transceiver module
  Soil Moisture Sensors

custom parts:
  NRF24L01: NRF24L01 module
